# Fritzing sketch BleSensorRemote (saved by Fritzing 0.9.3b)
breadboards: 1

parts:
  SparkFun_Pressure_Sensor_Breakout_-_MS5803-14BA1 = SparkFun Pressure Sensor Breakout - MS5803-14BA [part_number="SEN-12909 "]  # not connected
  Part1 = Adafruit Feather 32u4 Bluefruit [part_number="Adafruit #2829"]
  U1 = SWITCH_SPDT [package=kps-1290]

nets:
  N1: Part1.GND, U1.P
  N2: Part1.EN, U1.S

custom parts:
  SparkFun Pressure Sensor Breakout - MS5803-14BA: This is the MS5803-14BA Pressure Sensor Breakout, a high resolution pressure sensor with both an I2C and SPI interface. This MEMS pressure sensor measures the absolute pressure of the fluid around it which includes air, water, and anything else that acts like a viscous fluid. Depending on how you interpret the data, you can determine altitude, water depth, or any other tasks that require an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
  Adafruit Feather 32u4 Bluefruit: This is the Adafruit Feather 32u4 Bluefruit - our take on an 'all-in-one' Arduino-compatible + Bluetooth Low Energy with built in USB and battery charging. Its an Adafruit Feather 32u4 with a BTLE module, ready to rock! We have other boards in the Feather family, check'em out here. Bluetooth Low Energy is the hottest new low-power, 2.4GHz spectrum wireless protocol. In particular, its the only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
